# Fritzing sketch Ard-Bread-power-led-pin8 (saved by Fritzing 0.9.3b)
breadboards: 1

parts:
  Součástka1 = Arduino Uno (Rev3)
  R1 = Resistor [tolerance=±5% resistance=220 package=THT]
  LED1 = LED - 5mm [color="Red (633nm)" package="5 mm [THT]"]

nets:
  N1: Součástka1.D8, LED1.cathode
  N2: Součástka1.GND, R1.Pin_0
  N3: R1.Pin_1, LED1.anode
