# Fritzing sketch ard+dht+bmp+nrf (saved by Fritzing 0.9.3b)
breadboards: 1

parts:
  Součástka1 = Arduino Uno (Rev3)
  DHT1 = DHT11 Humitidy and Temperature Sensor
  Součástka2 = Barometric Pressure Sensor - BMP180 Breakout (GY-68)
  R1 = Resistor [tolerance=±5% resistance=220 package=THT]
  Součástka3 = NRF24L01+ Breakout Board

nets:
  N1: Součástka1.A4/SDA, Součástka2.SDA
  N2: Součástka1.A5/SCL, Součástka2.SCL
  N3: Součástka1.D9_PWM, Součástka3.CE
  N4: Součástka1.D10_PWM/SS, Součástka3.CS
  N5: Součástka1.D11_PWM/MOSI, Součástka3.MOSI
  N6: Součástka1.D12/MISO, Součástka3.MISO
  N7: Součástka1.D13/SCK, Součástka3.SCK
  GND: Součástka1.GND, DHT1.GND, Součástka2.GND, Součástka3.GND
  N8: Součástka1.D2, DHT1.DATA, R1.Pin_1
  3V3: Součástka1.3V3, Součástka3.VCC
  5V: Součástka1.5V, DHT1.VDD, Součástka2.VCC, R1.Pin_0

custom parts:
  DHT11 Humitidy and Temperature Sensor: DHT11 Humidity and Temperature Sensor
