# Fritzing sketch ard+nrf+oled (saved by Fritzing 0.9.3b)

parts:
  Součástka1 = Arduino Uno (Rev3)
  Součástka3 = NRF24L01+ Breakout Board
  Součástka4 = OLED Monochrome 128x64 1.3 inch [part_number=938]

nets:
  N1: Součástka1.A4/SDA, Součástka4.MOSI_SDA
  N2: Součástka1.A5/SCL, Součástka4.SCLK_SCK
  N3: Součástka1.D9_PWM, Součástka3.CE
  N4: Součástka1.D10_PWM/SS, Součástka3.CS
  N5: Součástka1.D11_PWM/MOSI, Součástka3.MOSI
  N6: Součástka1.D12/MISO, Součástka3.MISO
  N7: Součástka1.D13/SCK, Součástka3.SCK
  GND: Součástka1.GND, Součástka3.GND, Součástka4.GND
  3V3: Součástka1.3V3, Součástka3.VCC, Součástka4.3.3V

custom parts:
  OLED Monochrome 128x64 1.3 inch: These displays are small, only about 1.3" diagonal, but very readable due to the high contrast of an OLED display. This display is made of 128x64 individual white OLED pixels, each one is turned on or off by the controller chip. Because the display makes its own light, no backlight is required. This reduces the power required to run the OLED and is why the display has such high contrast; we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
