# Fritzing sketch ard+photores (saved by Fritzing 0.9.3b)
breadboards: 1

parts:
  R1 = Photocell (LDR) [package=THT]
  R2 = Resistor [tolerance=±5% resistance=220 package=THT]
  Součástka1 = Arduino Uno (Rev3)

nets:
  N1: R1.pin_0, R2.Pin_0, Součástka1.A0
  N2: R1.pin_1, Součástka1.5V
  N3: R2.Pin_1, Součástka1.GND
