# Fritzing sketch arduino-7400 (saved by Fritzing 0.9.3b)
breadboards: 1

parts:
  Součástka1 = Arduino Uno (Rev3)
  IC1 = IC, DIP package, 14 pins [chip_label=74HCT00]
  LED1 = LED - 5mm [color="Red (633nm)" package="5 mm [THT]"]
  R1 = Resistor [tolerance=±5% resistance=220 package=THT]

nets:
  N1: Součástka1.D2, IC1.pin1
  N2: Součástka1.D3_PWM, IC1.pin2
  N3: Součástka1.5V, IC1.pin14
  N4: Součástka1.GND, IC1.pin7, R1.Pin_1
  N5: IC1.pin3, LED1.anode
  N6: LED1.cathode, R1.Pin_0
