# Fritzing sketch atmega32-ard (saved by Fritzing 0.9.3b)
breadboards: 1

parts:
  IC1 = IC, DIP package, 40 pins [chip_label=ATmega32p]
  Součástka1 = FTDI Basic Programmer
  C1 = Ceramic Capacitor [capacitance=100nF package="200 mil [THT, multilayer]"]
  R1 = Resistor [tolerance=±5% resistance=220 package=THT]
  LED1 = LED - 5mm [color="Red (633nm)" package="5 mm [THT]"]
  R2 = Resistor [tolerance=±5% resistance=220 package=THT]

nets:
  N1: IC1.pin9, C1.0, R1.Pin_1
  N2: IC1.pin10, IC1.pin30, Součástka1.POWER, R1.Pin_0
  N3: IC1.pin11, IC1.pin31, Součástka1.GND, LED1.cathode
  N4: IC1.pin14, Součástka1.TXO
  N5: IC1.pin15, Součástka1.RXI
  N6: IC1.pin19, R2.Pin_1
  N7: Součástka1.DTR, C1.1
  N8: LED1.anode, R2.Pin_0
