# Fritzing sketch atmega32-boot (saved by Fritzing 0.9.3b)
breadboards: 1

parts:
  Součástka1 = Arduino Uno (Rev3)
  IC1 = IC, DIP package, 40 pins [chip_label=ATmega32p]

nets:
  N1: Součástka1.D10_PWM/SS, IC1.pin9
  N2: Součástka1.D11_PWM/MOSI, IC1.pin6
  N3: Součástka1.D12/MISO, IC1.pin7
  N4: Součástka1.D13/SCK, IC1.pin8
  N5: Součástka1.GND, IC1.pin11, IC1.pin31
  N6: Součástka1.5V, IC1.pin10, IC1.pin30
