# Fritzing sketch blinker (saved by Fritzing 0.9.3b)
breadboards: 1

parts:
  IC1 = IC, DIP package, 14 pins [chip_label=74LS04]
  LED1 = LED - 5mm [color="Red (633nm)" package="5 mm [THT]"]
  R1 = Resistor [tolerance=±5% resistance=330 package=THT]
  C1 = Electrolytic Capacitor [capacitance=1µF package="100 mil [THT, electrolytic]"]
  R2 = Resistor [tolerance=±5% resistance=10k package=THT]
  VCC1 = 4 x AAA Battery Mount

nets:
  N1: IC1.pin1, C1.-, R2.Pin_0
  N2: IC1.pin2, IC1.pin3, R2.Pin_1
  N3: IC1.pin4, IC1.pin5, C1.+
  N4: IC1.pin6, LED1.anode
  N5: IC1.pin7, R1.Pin_0, VCC1.-
  N6: IC1.pin14, VCC1.+
  N7: LED1.cathode, R1.Pin_1
