# Fritzing sketch esp+ard (saved by Fritzing 0.9.3b)

parts:
  U1 = ESP8266 WiFi Module [part_number=ESP8266]
  Součástka1 = Arduino Uno (Rev3)
  Součástka2 = Logic Level Converter

nets:
  N1: U1.RXD, Součástka2.TX2_LV
  VCC: U1.VCC, U1.CH_PD, Součástka1.3V3, Součástka2.LV
  GND: U1.GND, Součástka1.GND, Součástka2.GND
  N2: U1.TXD, Součástka2.RX2_LV
  N3: Součástka1.D0/RX, Součástka2.RX2_HV
  N4: Součástka1.D1/TX, Součástka2.TX2_HV
  N5: Součástka1.5V, Součástka2.HV

custom parts:
  ESP8266 WiFi Module: Generic WiFi Module based on the ESP8266 with onboard PCB antenna and UART communications
