# Fritzing sketch hc-sr04 (saved by Fritzing 0.9.3b)

parts:
  Součástka1 = Arduino Uno (Rev3)
  hc-sr1 = hc-sr04

nets:
  N1: Součástka1.D2, hc-sr1.Echo
  N2: Součástka1.D3_PWM, hc-sr1.Trig
  5V: Součástka1.5V, hc-sr1.VCC
  GND: Součástka1.GND, hc-sr1.GND
