# Fritzing sketch joystick+display (saved by Fritzing 0.9.3b)

parts:
  Součástka1 = Arduino Uno (Rev3)
  Součástka2 = Thumb Joystick
  Součástka3 = TFT 2.2 inch 320x240 w microSD [part_number=1480]

nets:
  N1: Součástka1.A0, Součástka2.HORZ
  N2: Součástka1.A1, Součástka2.VERT
  N3: Součástka1.D8, Součástka3.RESET
  N4: Součástka1.D9_PWM, Součástka3.DC
  N5: Součástka1.D10_PWM/SS, Součástka3.LCDCS
  N6: Součástka1.D11_PWM/MOSI, Součástka3.MOSI
  N7: Součástka1.D12/MISO, Součástka3.MISO
  N8: Součástka1.D13/SCK, Součástka3.SCLK
  N9: Součástka1.D6_PWM, Součástka2.SEL
  N10: Součástka1.3V3, Součástka3.BACKLIGHT
  5V: Součástka1.5V, Součástka2.VCC, Součástka3.VIN
  GND: Součástka1.GND, Součástka2.GND, Součástka3.GND

custom parts:
  TFT 2.2 inch 320x240 w microSD: This lovely little display breakout is the best way to add a small, colorful and bright display to any project. Since the display uses 4-wire SPI to communicate and has its own pixel-addressable frame buffer, it can be used with every kind of microcontroller. Even a very small one with low memory and few pins available! The 2.2" display has 320x240 color pixels.
