# Fritzing sketch joystick (saved by Fritzing 0.9.3b)

parts:
  Součástka1 = Arduino Uno (Rev3)
  Součástka2 = Thumb Joystick

nets:
  N1: Součástka1.A0, Součástka2.HORZ
  N2: Součástka1.A1, Součástka2.VERT
  N3: Součástka1.D8, Součástka2.SEL
  5V: Součástka1.5V, Součástka2.VCC
  GND: Součástka1.GND, Součástka2.GND
