# Fritzing sketch led+photores-neg (saved by Fritzing 0.9.3b)
breadboards: 1

parts:
  R1 = Photocell (LDR) [package=THT]
  LED1 = LED - 5mm [color="Red (633nm)" package="5 mm [THT]"]
  R2 = Resistor [tolerance=±5% resistance=220 package=THT]

nets:
  N1: R1.pin_0, LED1.anode, R2.Pin_0
  N2: R1.pin_1, LED1.cathode
