# Fritzing sketch pir+led (saved by Fritzing 0.9.3b)
breadboards: 1

parts:
  PIR1 = PIR sensor
  LED1 = LED - 5mm [color="Red (633nm)" package="5 mm [THT]"]
  R1 = Resistor [tolerance=±5% resistance=220 package=THT]
  Součástka1 = Breadboard Power Supply Board SMD

nets:
  VDD: PIR1.VDD, Součástka1.VCC
  N1: PIR1.SIG, LED1.anode
  GND: PIR1.GND, R1.Pin_1, Součástka1.GND
  N2: LED1.cathode, R1.Pin_0
