# Fritzing sketch rsff (saved by Fritzing 0.9.3b)
breadboards: 1

parts:
  LED1 = LED - 5mm [color="Red (633nm)" package="5 mm [THT]"]
  LED2 = LED - 5mm [color="Red (633nm)" package="5 mm [THT]"]
  R1 = Resistor [tolerance=±5% resistance=220 package=THT]
  R2 = Resistor [tolerance=±5% resistance=220 package=THT]
  S1 = Toggle Switch [package=THT]
  S2 = Toggle Switch [package=THT]
  IC1 = IC, DIP package, 14 pins [chip_label=74LS02]  # not connected

nets:
  N1: LED1.anode, R2.Pin_0
  N2: LED2.anode, R1.Pin_0
  N3: R1.Pin_1, R2.Pin_1
  N4: S1.L1, S2.L1
  N5: S1.L2, S2.L2
