# Fritzing sketch sensor bjt (saved by Fritzing 0.9.3b)
breadboards: 1

parts:
  Q1 = NPN-Transistor [package="TO92 [THT]"]
  VCC1 = 4 x AAA Battery Mount
  R1 = Resistor [tolerance=±5% resistance=220 package=THT]
  LED1 = LED - 5mm [color="Red (633nm)" package="5 mm [THT]"]

nets:
  N1: Q1.E, VCC1.-
  N2: Q1.C, LED1.cathode
  N3: VCC1.+, R1.Pin_1
  N4: R1.Pin_0, LED1.anode
